// Logisim project Basic_logicgates.circ as structural Verilog: 1 circuit, main circuit main
module main (
  input  in_1,
  input  in_2,
  input  in_3,
  input  in_4,
  input  in_5,
  input  in_6,
  input  in_7,
  input  in_8,
  input  in_9,
  input  in_10,
  input  in_11,
  input  in_12,
  input  in_13,
  input  in_14,
  input  in_15,
  output out_16,
  output out_17,
  output out_18,
  output out_19,
  output out_20,
  output out_21,
  output out_22,
  output out_23,
  output out_24
);

  and and_1 (out_16, in_1, in_4);
  nand nand_1 (out_21, in_8, in_11);
  xor xor_1 (out_22, in_12, in_14);
  or or_1 (out_17, in_2, in_5);
  nor nor_1 (out_20, in_7, in_10);
  xor xor_2 (out_23, in_13, in_15);
  and and_2 (out_24, in_15, in_13);
  not not_1 (out_18, in_3);
  xnor xnor_1 (out_19, in_6, in_9);
endmodule
